// Logisim project IT012_Lab01_25520717.circ as structural Verilog: 6 circuits, main circuit Warmup
module Warmup (
  input  A,
  input  B,
  output F
);

  wire not_1_out;

  not not_1 (not_1_out, B);
  and and_1 (F, A, not_1_out);
endmodule

module TN1 (
  input  A,
  input  B,
  input  C,
  output NOT,
  output AND,
  output OR,
  output NAND,
  output NOR,
  output XOR,
  output XNOR,
  output CHAIN
);

  wire nand_2_out;

  not not_1 (NOT, A);
  and and_1 (AND, A, B);
  or or_1 (OR, A, B);
  nand nand_1 (NAND, A, C, B);
  nor nor_1 (NOR, A, B);
  xor xor_1 (XOR, A, C, B);
  xnor xnor_1 (XNOR, A, B);
  nand nand_2 (nand_2_out, A, B);
  nand nand_3 (CHAIN, nand_2_out, C);
endmodule

module TN2 (
  input  x,
  input  y,
  input  z,
  output EQ1,
  output EQ2,
  output EQ3,
  output EQ4,
  output EQ5
);

  wire and_1_out, and_2_out, and_3_out, and_4_out, and_5_out, not_1_out, not_2_out, not_3_out, not_4_out,
       or_1_out, or_2_out, or_3_out, or_4_out, or_5_out, or_6_out;

  not not_1 (not_1_out, x);
  not not_2 (not_2_out, y);
  and and_1 (and_1_out, y, z);
  or or_1 (or_1_out, x, y);
  or or_2 (or_2_out, x, z);
  or or_3 (or_3_out, and_1_out, x);
  and and_2 (and_2_out, not_1_out, y);
  or or_4 (or_4_out, x, y);
  and and_3 (and_3_out, not_1_out, not_2_out);
  and and_4 (and_4_out, x, y);
  not not_3 (not_3_out, and_4_out);
  and and_5 (and_5_out, or_1_out, or_2_out);
  or or_5 (or_5_out, and_2_out, x);
  or or_6 (or_6_out, x, y);
  not not_4 (not_4_out, or_4_out);
  xnor xnor_1 (EQ1, not_4_out, and_3_out);
  xnor xnor_2 (EQ2, and_3_out, not_3_out);
  xnor xnor_3 (EQ3, or_3_out, and_5_out);
  xnor xnor_4 (EQ4, x, or_5_out);
  xnor xnor_5 (EQ5, or_5_out, or_6_out);
endmodule

module TN3 (
  input  A,
  input  B,
  input  C,
  input  D,
  output F
);

  wire and_1_out, and_2_out, and_3_out, and_4_out, and_5_out, and_6_out, not_1_out, not_2_out, not_3_out,
       not_4_out;

  not not_1 (not_1_out, A);
  not not_2 (not_2_out, B);
  not not_3 (not_3_out, C);
  not not_4 (not_4_out, D);
  and and_1 (and_1_out, not_1_out, not_2_out, C, not_4_out);
  and and_2 (and_2_out, not_1_out, not_2_out, C, D);
  and and_3 (and_3_out, not_1_out, B, not_3_out, D);
  and and_4 (and_4_out, not_1_out, B, C, D);
  and and_5 (and_5_out, A, not_2_out, C, D);
  and and_6 (and_6_out, A, B, not_3_out, D);
  or or_1 (F, and_1_out, and_2_out, and_3_out, and_4_out, and_5_out, and_6_out);
endmodule

module TN4 (
  input  A,
  input  B,
  input  C,
  input  D,
  output F_can,
  output EQ1,
  output EQ2
);

  wire and_1_out, and_2_out, and_3_out, and_4_out, and_5_out, and_6_out, and_7_out, and_8_out, and_9_out,
       and_10_out, F_pos_out, F_sop_out, not_1_out, not_2_out, not_3_out, not_4_out, or_1_out, or_2_out,
       or_3_out, or_4_out;

  not not_1 (not_1_out, A);
  not not_2 (not_2_out, B);
  not not_3 (not_3_out, C);
  not not_4 (not_4_out, D);
  and and_1 (and_1_out, not_1_out, not_2_out, C, not_4_out);
  and and_2 (and_2_out, not_1_out, not_2_out, C, D);
  and and_3 (and_3_out, not_1_out, B, not_3_out, D);
  and and_4 (and_4_out, not_1_out, B, C, D);
  and and_5 (and_5_out, A, not_2_out, C, D);
  and and_6 (and_6_out, A, B, not_3_out, D);
  and and_7 (and_7_out, not_1_out, not_2_out, C);
  and and_8 (and_8_out, not_2_out, C, D);
  and and_9 (and_9_out, not_1_out, B, D);
  and and_10 (and_10_out, B, not_3_out, D);
  or or_1 (or_1_out, not_1_out, D);
  or or_2 (or_2_out, B, C);
  or or_3 (or_3_out, not_2_out, D);
  or or_4 (or_4_out, not_1_out, not_2_out, not_3_out);
  or u_F_can (F_can, and_1_out, and_2_out, and_3_out, and_4_out, and_5_out, and_6_out);
  or F_sop (F_sop_out, and_7_out, and_8_out, and_9_out, and_10_out);
  and F_pos (F_pos_out, or_1_out, or_2_out, or_3_out, or_4_out);
  xnor xnor_1 (EQ1, F_can, F_sop_out);
  xnor xnor_2 (EQ2, F_can, F_pos_out);
endmodule

module TN5 (
  input  A,
  input  B,
  input  C,
  output F
);

  wire xor_1_out;

  xor xor_1 (xor_1_out, A, B);
  xor xor_2 (F, xor_1_out, C);
endmodule
